// Logisim project adnan_maleskic_21042.circ as structural Verilog: 6 circuits, main circuit main
module main (
  input  PCRESET,
  input  RSTMEM
);

  wire and_1_out, clock_1_out, mainctrl_1_beq, mainctrl_1_bne, mainctrl_1_extop, mainctrl_1_j,
       mainctrl_1_jal, mainctrl_1_ld, mainctrl_1_st, mainctrl_1_we, nextpc_1_pcsrc, nor_1_out, nor_2_out,
       or_1_out;
  wire [3:0] functalu_1_a0, multiplexer_7_out, opalu_1_a0;
  wire [4:0] multiplexer_4_out, multiplexer_5_out;
  wire [5:0] undriven;
  wire [15:0] undriven_2;
  wire [25:16] registerfile_1_p6;
  wire [29:0] incrementer_1_p2, multiplexer_1_out, nextpc_1_npc;
  wire [31:0] inputext_1_o, mips_alu_1_p5, mips_ram_1_p5, multiplexer_2_out, multiplexer_3_out,
       multiplexer_6_out, multiplexer_8_out, register_1_q, registerfile_1_p7, registerfile_1_p8;

  Multiplexer #(.width(30), .enable("false")) multiplexer_1 (
    .in0(incrementer_1_p2), .in1(nextpc_1_npc), .out(multiplexer_1_out), .sel(nextpc_1_pcsrc));
  Clock clock_1 (.out(clock_1_out));
  Register #(.width(32), .trigger("falling")) register_1 (
    .D(multiplexer_2_out), .en(1'b1), .clk(clock_1_out), .Q(register_1_q), .clr(PCRESET));
  Multiplexer #(.width(32), .enable("false")) multiplexer_2 (
    .in0({multiplexer_1_out, 2'b00}), .in1(registerfile_1_p7), .out(multiplexer_2_out), .sel(and_1_out));
  // Incrementer #(.width(30)) incrementer_1: pin names not known; wires that end beside it: register_1_q[31:2], incrementer_1_p2, register_1_q
  mainCtrl mainctrl_1 (
    .Op5(undriven[5]), .Op4(undriven[4]), .Op3(undriven[3]), .Op2(undriven[2]), .Op1(undriven[1]),
    .Op0(undriven[0]), .WE(mainctrl_1_we), .St(mainctrl_1_st), .Ld(mainctrl_1_ld), .Beq(mainctrl_1_beq),
    .Bne(mainctrl_1_bne), .J(mainctrl_1_j), .Jal(mainctrl_1_jal), .ExtOp(mainctrl_1_extop));
  opALU opalu_1 (
    .Op5(undriven[5]), .Op4(undriven[4]), .Op3(undriven[3]), .Op2(undriven[2]), .Op1(undriven[1]),
    .Op0(undriven[0]), .A3(opalu_1_a0[3]), .A2(opalu_1_a0[2]), .A1(opalu_1_a0[1]), .A0(opalu_1_a0[0]));
  // MIPSProgramROM mipsprogramrom_1: pin names not known
  nor nor_1 (nor_1_out, undriven[0], undriven[1], undriven[2], undriven[3], undriven[4], undriven[5]);
  Multiplexer #(.width(32), .enable("false")) multiplexer_3 (
    .in0(multiplexer_8_out), .in1({incrementer_1_p2, 2'b00}), .out(multiplexer_3_out), .sel(mainctrl_1_jal));
  nor nor_2 (nor_2_out, undriven_2[5], undriven_2[4], ~undriven_2[3], undriven_2[2], undriven_2[1], undriven_2[0]);  // NOR_Gate
  Multiplexer #(.width(5), .enable("false")) multiplexer_4 (
    .in0(multiplexer_5_out), .in1({5{1'b1}}), .out(multiplexer_4_out), .sel(mainctrl_1_jal));
  Multiplexer #(.width(5), .enable("false")) multiplexer_5 (
    .in0(registerfile_1_p6[20:16]), .in1(undriven_2[15:11]), .out(multiplexer_5_out), .sel(nor_1_out));
  or or_1 (or_1_out, mainctrl_1_we, nor_1_out);
  functALU functalu_1 (
    .F5(undriven_2[5]), .F4(undriven_2[4]), .F3(undriven_2[3]), .F2(undriven_2[2]), .F1(undriven_2[1]),
    .F0(undriven_2[0]), .A3(functalu_1_a0[3]), .A2(functalu_1_a0[2]), .A1(functalu_1_a0[1]),
    .A0(functalu_1_a0[0]));
  and and_1 (and_1_out, nor_1_out, nor_2_out);
  // RegisterFile #(.trigger("falling")) registerfile_1: pin names not known; wires that end beside it: multiplexer_3_out, clock_1_out, or_1_out, multiplexer_4_out, registerfile_1_p6[25:21], registerfile_1_p6[20:16], registerfile_1_p7, registerfile_1_p8
  nextPC nextpc_1 (
    .IncPC(incrementer_1_p2), .Imm26({registerfile_1_p6, undriven_2}), .J(mainctrl_1_j),
    .Beq(mainctrl_1_beq), .Bne(mainctrl_1_bne), .Zero(mips_alu_1_p5), .nPC(nextpc_1_npc),
    .PCsrc(nextpc_1_pcsrc));
  Multiplexer #(.width(32), .enable("false")) multiplexer_6 (
    .in0(inputext_1_o), .in1(registerfile_1_p8), .out(multiplexer_6_out), .sel(nor_1_out));
  inputExt inputext_1 (.sign(mainctrl_1_extop), .A(undriven_2), .O(inputext_1_o));
  Multiplexer #(.width(4), .enable("false")) multiplexer_7 (
    .in0(opalu_1_a0), .in1(functalu_1_a0), .out(multiplexer_7_out), .sel(nor_1_out));
  // Mips_ALU mips_alu_1: pin names not known; wires that end beside it: registerfile_1_p7, multiplexer_6_out, multiplexer_7_out, undriven_2[10:6], mips_alu_1_p5, mips_alu_1_p5[19:0], registerfile_1_p8
  Multiplexer #(.width(32), .enable("false")) multiplexer_8 (
    .in0(mips_alu_1_p5), .in1(mips_ram_1_p5), .out(multiplexer_8_out), .sel(mainctrl_1_ld));
  // MIPS_RAM mips_ram_1: pin names not known; wires that end beside it: mainctrl_1_st, clock_1_out, mainctrl_1_ld, RSTMEM, mips_ram_1_p5

  // Notes on the sheet:
  //   contents of mipsprogramrom_1 (hex, n*v repeats v):
  //   funkcija: subu $2, $4, $5 jr $31  main: addiu $8, $0, 4 ori $9, $0, 0xabcd sll $9, $9, 16 ori $9,
  //   $9, 0x1234 sw $9, 0($8) sw $9, 4($8) ori $10, $0, 4 addu $12, $8, $10 lw $13, 0($12) addu $5, $0,
  //   $13 bne   $5, $0, razlicito addiu $4, $5, -8 j     krajif razlicito: addiu $4, $5, 8 krajif:  jal
  //   funkcija sw $2, 8($8)  # Nakon izvrsenja programa u RAM memoriji bi trebalo da budu podaci: # adresa
  //   0: 0xabcd1234 # adresa 4: 0xabcd1234 # adresa 8: 0x00000008 # Ako je na adresi 8 vrijednost
  //   0xfffffff8 onda branch ne radi kako bi trebalo
endmodule

module functALU (
  input  F5,
  input  F4,
  input  F3,
  input  F2,
  input  F1,
  input  F0,
  output A3,
  output A2,
  output A1,
  output A0
);

  wire not_1_out;

  and and_1 (A1, F5, F0);
  not not_1 (not_1_out, F5);
  and and_2 (A0, not_1_out, F0);

  assign A2 = F1;
  assign A3 = F2;
endmodule

module mainCtrl (
  input  Op5,
  input  Op4,
  input  Op3,
  input  Op2,
  input  Op1,
  input  Op0,
  output WE,
  output St,
  output Ld,
  output Beq,
  output Bne,
  output J,
  output Jal,
  output ExtOp
);

  wire and_2_out, and_3_out, and_9_out, and_10_out, not_1_out, not_2_out, not_3_out, not_4_out, not_5_out,
       not_6_out, not_7_out, not_8_out, not_9_out, not_10_out, not_11_out, not_12_out, not_13_out,
       not_14_out, not_15_out, not_16_out, not_17_out;

  not not_1 (not_1_out, Op3);
  not not_2 (not_2_out, Op5);
  and and_1 (St, Op5, Op3);
  not not_3 (not_3_out, Op3);
  not not_4 (not_4_out, Op3);
  not not_5 (not_5_out, Op0);
  not not_6 (not_6_out, Op3);
  not not_7 (not_7_out, Op1);
  not not_8 (not_8_out, Op5);
  not not_9 (not_9_out, Op4);
  not not_10 (not_10_out, Op3);
  not not_11 (not_11_out, Op2);
  not not_12 (not_12_out, Op5);
  not not_13 (not_13_out, Op4);
  not not_14 (not_14_out, Op3);
  not not_15 (not_15_out, Op2);
  not not_16 (not_16_out, Op2);
  not not_17 (not_17_out, Op3);
  and and_2 (and_2_out, not_1_out, Op1);
  and and_3 (and_3_out, not_2_out, Op3);
  and and_4 (Ld, Op5, not_3_out);
  and and_5 (Beq, not_4_out, Op2, not_5_out);
  and and_6 (Bne, not_6_out, not_7_out, Op0);
  and and_7 (J, not_8_out, not_9_out, not_10_out, not_11_out, Op1);
  and and_8 (Jal, not_12_out, not_13_out, not_14_out, not_15_out, Op1, Op0);
  and and_9 (and_9_out, not_16_out, Op0);
  and and_10 (and_10_out, not_17_out, Op2);
  or or_1 (WE, and_2_out, and_3_out);
  or or_2 (ExtOp, and_9_out, and_10_out);
endmodule

module opALU (
  input  Op5,
  input  Op4,
  input  Op3,
  input  Op2,
  input  Op1,
  input  Op0,
  output A3,
  output A2,
  output A1,
  output A0
);

  wire and_2_out, and_3_out, not_1_out, not_2_out, not_3_out, not_4_out;

  and and_1 (A3, Op3, Op2);
  not not_1 (not_1_out, Op3);
  not not_2 (not_2_out, Op1);
  not not_3 (not_3_out, Op0);
  not not_4 (not_4_out, Op3);
  and and_2 (and_2_out, not_1_out, not_2_out);
  and and_3 (and_3_out, Op1, not_3_out);
  or or_1 (A1, not_4_out, Op0);
  or or_2 (A2, and_2_out, and_3_out);

  assign A0 = 1'b0;
endmodule

module inputExt (
  input  sign,
  input  [15:0] A,
  output [31:0] O
);

  and and_1 (O[31], sign, A[15]);

  assign O[30:0] = {{15{O[31]}}, A};
endmodule

module nextPC (
  input  [29:0] IncPC,
  input  [25:0] Imm26,
  input  J,
  input  Beq,
  input  Bne,
  input  [31:0] Zero,
  output [29:0] nPC,
  output PCsrc
);

  wire and_1_out, and_2_out, or_1_out;
  wire [29:0] adder_1_out, bit_extender_1_out;

  assign bit_extender_1_out = {{14{Imm26[15]}}, Imm26[15:0]};  // Bit_Extender bit_extender_1
  Adder #(.width(30)) adder_1 (.a(IncPC), .b(bit_extender_1_out), .out(adder_1_out));  // open: cin, cout
  Multiplexer #(.width(30), .enable("false")) multiplexer_1 (
    .in0(adder_1_out), .in1({IncPC[29:26], Imm26}), .out(nPC), .sel(J));
  or or_1 (or_1_out, Zero[31], Zero[30], Zero[29], Zero[28], Zero[27], Zero[26], Zero[25], Zero[24], Zero[23], Zero[22], Zero[21], Zero[20], Zero[19], Zero[18], Zero[17], Zero[16], Zero[14], Zero[13], Zero[12], Zero[11], Zero[10], Zero[9], Zero[8], Zero[7], Zero[6], Zero[5], Zero[4], Zero[3], Zero[2], Zero[1], Zero[0], Zero[15]);
  or or_2 (PCsrc, and_1_out, J, and_2_out);
  and and_1 (and_1_out, ~or_1_out, Beq);  // AND_Gate
  and and_2 (and_2_out, or_1_out, Bne);
endmodule
