// Logisim project nasiofhs.circ as structural Verilog
module main (
  input  A,
  input  B,
  input  S,
  output O
);

  wire and_1_out, and_2_out;

  and and_1 (and_1_out, A, S);
  and and_2 (and_2_out, B, ~S);  // AND_Gate
  or or_1 (O, and_1_out, and_2_out);
endmodule

module mux21 (
  input  A,
  input  B,
  input  S,
  output O
);

  wire and_1_out, and_2_out, not_1_out;

  not not_1 (not_1_out, S);
  and and_1 (and_1_out, B, S);
  and and_2 (and_2_out, A, not_1_out);
  or or_1 (O, and_1_out, and_2_out);
endmodule

module mux41 (
  input  in_1,
  input  in_2,
  input  in_3,
  input  in_4,
  input  [1:0] in_5,
  output out_6
);

  wire mux21_1_o, mux21_2_o;

  mux21 mux21_1 (.A(in_1), .B(in_2), .S(in_5[0]), .O(mux21_1_o));
  mux21 mux21_2 (.A(in_3), .B(in_4), .S(in_5[0]), .O(mux21_2_o));
  mux21 mux21_3 (.A(mux21_1_o), .B(mux21_2_o), .S(in_5[1]), .O(out_6));
endmodule

module rslatch (
  input  R,
  input  S,
  output Q,
  output out_4
);

  nor nor_1 (Q, R, out_4);
  nor nor_2 (out_4, Q, S);
endmodule

module dlatch (
  input  C,
  input  D,
  output Q
);

  wire and_1_out, and_2_out;

  and and_1 (and_1_out, C, ~D);  // AND_Gate
  and and_2 (and_2_out, C, D);
  rslatch rslatch_1 (.R(and_1_out), .S(and_2_out), .Q(Q));  // open: out_4
endmodule

module dflipflop (
  input  C,
  input  D,
  output Q
);

  wire dlatch_1_q, not_1_out;

  not not_1 (not_1_out, C);
  dlatch dlatch_1 (.C(C), .D(D), .Q(dlatch_1_q));
  dlatch dlatch_2 (.C(not_1_out), .D(dlatch_1_q), .Q(Q));
endmodule

module register4bit (
  input  [3:0] reginput,
  input  C,
  input  WE,
  output [3:0] Q
);

  wire and_1_out;

  and and_1 (and_1_out, C, WE);
  dflipflop dflipflop_1 (.C(and_1_out), .D(reginput[0]), .Q(Q[0]));
  dflipflop dflipflop_2 (.C(and_1_out), .D(reginput[1]), .Q(Q[1]));
  dflipflop dflipflop_3 (.C(and_1_out), .D(reginput[2]), .Q(Q[2]));
  dflipflop dflipflop_4 (.C(and_1_out), .D(reginput[3]), .Q(Q[3]));
endmodule

module registerfile4 (
  input  [3:0] in_1,
  input  [1:0] RA,
  input  [1:0] RB,
  input  [1:0] RW,
  input  C,
  input  WE,
  input  [3:0] BUSW,
  output [3:0] BUSA,
  output [3:0] BUSB
);

  wire and_1_out, and_2_out, and_3_out, decoder_1_out0, decoder_1_out1, decoder_1_out2, decoder_1_out3,
       decoder_2_out0, decoder_2_out1, decoder_2_out2, decoder_2_out3, decoder_3_out0, decoder_3_out1,
       decoder_3_out2, decoder_3_out3;
  wire [3:0] register4bit_1_q, register4bit_2_q, register4bit_3_q;

  Decoder #(.select(2)) decoder_1 (
    .out0(decoder_1_out0), .out1(decoder_1_out1), .out2(decoder_1_out2), .out3(decoder_1_out3), .sel(RW));  // open: en
  Decoder #(.select(2)) decoder_2 (
    .out0(decoder_2_out0), .out1(decoder_2_out1), .out2(decoder_2_out2), .out3(decoder_2_out3), .sel(RA));  // open: en
  Decoder #(.select(2)) decoder_3 (
    .out0(decoder_3_out0), .out1(decoder_3_out1), .out2(decoder_3_out2), .out3(decoder_3_out3), .sel(RB));  // open: en
  and and_1 (and_1_out, decoder_1_out1, WE);
  and and_2 (and_2_out, decoder_1_out2, WE);
  and and_3 (and_3_out, decoder_1_out3, WE);
  assign BUSA = decoder_2_out0 ? in_1 : 4'bz;  // Controlled_Buffer controlled_buffer_1
  assign BUSB = decoder_3_out0 ? in_1 : 4'bz;  // Controlled_Buffer controlled_buffer_2
  register4bit register4bit_1 (.reginput(BUSW), .C(C), .WE(and_1_out), .Q(register4bit_1_q));
  register4bit register4bit_2 (.reginput(BUSW), .C(C), .WE(and_2_out), .Q(register4bit_2_q));
  register4bit register4bit_3 (.reginput(BUSW), .C(C), .WE(and_3_out), .Q(register4bit_3_q));
  assign BUSA = decoder_2_out1 ? register4bit_1_q : 4'bz;  // Controlled_Buffer controlled_buffer_3
  assign BUSB = decoder_3_out1 ? register4bit_1_q : 4'bz;  // Controlled_Buffer controlled_buffer_4
  assign BUSA = decoder_2_out2 ? register4bit_2_q : 4'bz;  // Controlled_Buffer controlled_buffer_5
  assign BUSB = decoder_3_out2 ? register4bit_2_q : 4'bz;  // Controlled_Buffer controlled_buffer_6
  assign BUSA = decoder_2_out3 ? register4bit_3_q : 4'bz;  // Controlled_Buffer controlled_buffer_7
  assign BUSB = decoder_3_out3 ? register4bit_3_q : 4'bz;  // Controlled_Buffer controlled_buffer_8
  // also tied to GND on the sheet: decoder_1_out0
endmodule
