// Logisim project jinasfl.circ as structural Verilog: 6 circuits, main circuit main
module main (
  input  [7:0] in_1,
  input  [7:0] in_2,
  output out_3,
  output [7:0] out_4
);

  add8b add8b_1 (.S(out_4), .Co(out_3), .B(in_2), .A(in_1));  // open: Cin
endmodule

module add1b (
  input  A,
  input  B,
  input  Cin,
  output S,
  output Co
);

  wire and_1_out, and_2_out, and_3_out, and_4_out, and_5_out, and_6_out, and_7_out, not_1_out, not_2_out,
       not_3_out, not_4_out, not_5_out, not_6_out;

  not not_1 (not_1_out, A);
  not not_2 (not_2_out, B);
  not not_3 (not_3_out, A);
  not not_4 (not_4_out, Cin);
  not not_5 (not_5_out, B);
  not not_6 (not_6_out, Cin);
  and and_1 (and_1_out, B, Cin);
  and and_2 (and_2_out, A, Cin);
  and and_3 (and_3_out, A, B);
  and and_4 (and_4_out, not_1_out, not_2_out, Cin);
  and and_5 (and_5_out, not_3_out, B, not_4_out);
  and and_6 (and_6_out, A, not_5_out, not_6_out);
  and and_7 (and_7_out, A, B, Cin);
  or or_1 (Co, and_1_out, and_2_out, and_3_out);
  or or_2 (S, and_4_out, and_5_out, and_6_out, and_7_out);
endmodule

module add8b (
  input  [7:0] A,
  input  [7:0] B,
  input  Cin,
  output Co,
  output [7:0] S
);

  wire add1b_2_co, add1b_3_co, add1b_4_co, add1b_5_co, add1b_6_co, add1b_7_co, add1b_8_co;

  add1b add1b_1 (.Co(Co), .S(S[7]), .Cin(add1b_2_co), .B(B[7]), .A(A[7]));
  add1b add1b_2 (.Co(add1b_2_co), .S(S[6]), .Cin(add1b_3_co), .B(B[6]), .A(A[6]));
  add1b add1b_3 (.Co(add1b_3_co), .S(S[5]), .Cin(add1b_4_co), .B(B[5]), .A(A[5]));
  add1b add1b_4 (.Co(add1b_4_co), .S(S[4]), .Cin(add1b_5_co), .B(B[4]), .A(A[4]));
  add1b add1b_5 (.Co(add1b_5_co), .S(S[3]), .Cin(add1b_6_co), .B(B[3]), .A(A[3]));
  add1b add1b_6 (.Co(add1b_6_co), .S(S[2]), .Cin(add1b_7_co), .B(B[2]), .A(A[2]));
  add1b add1b_7 (.Co(add1b_7_co), .S(S[1]), .Cin(add1b_8_co), .B(B[1]), .A(A[1]));
  add1b add1b_8 (.Co(add1b_8_co), .S(S[0]), .Cin(Cin), .B(B[0]), .A(A[0]));
endmodule

module alu8b (
  input  [7:0] A,
  input  [7:0] B,
  input  [3:0] Op,
  output [7:0] C
);

  wire aluctrl_1_t, aluctrl_1_y;
  wire [1:0] aluctrl_1_x0;
  wire [7:0] add8b_1_s, and_1_out, bit_extender_1_out, multiplexer_1_out, nor_1_out, or_1_out, xor_1_out,
       xor_2_out;

  assign xor_1_out = B ^ bit_extender_1_out;  // XOR_Gate xor_1, 8 bits wide
  assign bit_extender_1_out = {{7{aluctrl_1_t}}, aluctrl_1_t};  // Bit_Extender bit_extender_1
  // Probe on aluctrl_1_t
  aluctrl aluctrl_1 (.in_1(Op), .T(aluctrl_1_t), .X1(aluctrl_1_x0[1]), .X0(aluctrl_1_x0[0]), .Y(aluctrl_1_y));
  add8b add8b_1 (.S(add8b_1_s), .Cin(aluctrl_1_t), .B(xor_1_out), .A(A));  // open: Co
  assign and_1_out = A & B;  // AND_Gate and_1, 8 bits wide
  assign or_1_out = A | B;  // OR_Gate or_1, 8 bits wide
  assign xor_2_out = A ^ B;  // XOR_Gate xor_2, 8 bits wide
  assign nor_1_out = ~(A | B);  // NOR_Gate nor_1, 8 bits wide
  Multiplexer #(.select(2), .width(8), .enable("false")) multiplexer_1 (
    .in0(and_1_out), .in1(or_1_out), .in2(xor_2_out), .in3(nor_1_out), .out(multiplexer_1_out),
    .sel(aluctrl_1_x0));
  // Probe on aluctrl_1_x0
  Multiplexer #(.width(8), .enable("false")) multiplexer_2 (
    .in0(add8b_1_s), .in1(multiplexer_1_out), .out(C), .sel(aluctrl_1_y));
  // Probe on aluctrl_1_y
endmodule

module aluctrl (
  input  [3:0] in_1,
  output T,
  output X1,
  output X0,
  output Y
);


  assign T = in_1[2];
  assign X0 = in_1[1];
  assign X1 = in_1[2];
  assign Y = in_1[3];
endmodule

module idk (
);

  // MIPSProgramROM mipsprogramrom_1: pin names not known
  // RegisterFile registerfile_1: pin names not known
  // Mips_ALU mips_alu_1: pin names not known
  // MIPS_RAM mips_ram_1: pin names not known
endmodule
