// Logisim project projekat.circ as structural Verilog: 5 circuits, main circuit main
module main (
  input  PCRESET,
  input  RSTMEM
);

  wire clock_1_out, mainctrl_1_extop, mainctrl_1_ld, mainctrl_1_st, mainctrl_1_we, nor_1_out, or_1_out,
       registerfile_1_p6;
  wire [3:0] functalu_1_a0, mips_alu_1_p3, opalu_1_a0;
  wire [4:0] multiplexer_1_out;
  wire [5:0] undriven;
  wire [25:0] registerfile_1_p5;
  wire [29:0] incrementer_1_p2;
  wire [31:0] inputext_1_o, mips_alu_1_p2, mips_alu_1_p5, mips_ram_1_p5, register_1_q, registerfile_1_p1,
       registerfile_1_p7;

  Register #(.width(32), .trigger("falling")) register_1 (
    .D({incrementer_1_p2, 2'b00}), .en(1'b1), .clk(clock_1_out), .Q(register_1_q), .clr(PCRESET));
  Clock clock_1 (.out(clock_1_out));
  // Incrementer #(.width(30)) incrementer_1: pin names not known; wires that end beside it: register_1_q[31:2], incrementer_1_p2, register_1_q
  mainCtrl mainctrl_1 (
    .Op5(undriven[5]), .Op4(undriven[4]), .Op3(undriven[3]), .Op2(undriven[2]), .Op1(undriven[1]),
    .Op0(undriven[0]), .WE(mainctrl_1_we), .St(mainctrl_1_st), .Ld(mainctrl_1_ld), .ExtOp(mainctrl_1_extop));  // open: Beq, Bne, J
  opALU opalu_1 (
    .Op5(undriven[5]), .Op4(undriven[4]), .Op3(undriven[3]), .Op2(undriven[2]), .Op1(undriven[1]),
    .Op0(undriven[0]), .A3(opalu_1_a0[3]), .A2(opalu_1_a0[2]), .A1(opalu_1_a0[1]), .A0(opalu_1_a0[0]));
  // MIPSProgramROM mipsprogramrom_1: pin names not known; wires that end beside it: clock_1_out
  nor nor_1 (nor_1_out, undriven[0], undriven[1], undriven[2], undriven[3], undriven[4], undriven[5]);
  or or_1 (or_1_out, mainctrl_1_we, nor_1_out);
  functALU functalu_1 (
    .F5(registerfile_1_p5[5]), .F4(registerfile_1_p5[4]), .F3(registerfile_1_p5[3]),
    .F2(registerfile_1_p5[2]), .F1(registerfile_1_p5[1]), .F0(registerfile_1_p5[0]), .A3(functalu_1_a0[3]),
    .A2(functalu_1_a0[2]), .A1(functalu_1_a0[1]), .A0(functalu_1_a0[0]));
  Multiplexer #(.width(5), .enable("false")) multiplexer_1 (
    .in0(registerfile_1_p5[20:16]), .in1(registerfile_1_p5[15:11]), .out(multiplexer_1_out), .sel(nor_1_out));
  // RegisterFile #(.trigger("falling")) registerfile_1: pin names not known; wires that end beside it: registerfile_1_p1, or_1_out, multiplexer_1_out, registerfile_1_p5[25:21], registerfile_1_p5[20:16], registerfile_1_p6, registerfile_1_p7
  inputExt inputext_1 (.sign(mainctrl_1_extop), .A(registerfile_1_p5[15:0]), .O(inputext_1_o));
  // Mips_ALU mips_alu_1: pin names not known; wires that end beside it: registerfile_1_p6, mips_alu_1_p2, mips_alu_1_p3, registerfile_1_p5[10:6], mips_alu_1_p5, mips_alu_1_p5[19:0], registerfile_1_p7
  Multiplexer #(.width(32), .enable("false")) multiplexer_2 (
    .in0(inputext_1_o), .in1(registerfile_1_p7), .out(mips_alu_1_p2), .sel(nor_1_out));
  Multiplexer #(.width(32), .enable("false")) multiplexer_3 (
    .in0(mips_alu_1_p5), .in1(mips_ram_1_p5), .out(registerfile_1_p1), .sel(mainctrl_1_ld));
  Multiplexer #(.width(4), .enable("false")) multiplexer_4 (
    .in0(opalu_1_a0), .in1(functalu_1_a0), .out(mips_alu_1_p3), .sel(nor_1_out));
  // Probe on mips_alu_1_p5
  // MIPS_RAM mips_ram_1: pin names not known; wires that end beside it: mainctrl_1_st, clock_1_out, mainctrl_1_ld, RSTMEM, mips_ram_1_p5

  // Notes on the sheet:
  //   contents of mipsprogramrom_1 (hex, n*v repeats v):
  //   funkcija: subu $2, $4, $5 jr $31  main: addiu $8, $0, 4 ori $9, $0, 0xabcd sll $9, $9, 16 ori $9,
  //   $9, 0x1234 sw $9, 0($8) sw $9, 4($8) ori $10, $0, 4 addu $12, $8, $10 lw $13, 0($12) addu $5, $0,
  //   $13 addiu $4, $5, 8 jal funkcija sw $2, 8($8)
endmodule

module functALU (
  input  F5,
  input  F4,
  input  F3,
  input  F2,
  input  F1,
  input  F0,
  output A3,
  output A2,
  output A1,
  output A0
);

  wire not_1_out;

  and and_1 (A1, F5, F0);
  not not_1 (not_1_out, F5);
  and and_2 (A0, not_1_out, F0);

  assign A2 = F1;
  assign A3 = F2;
endmodule

module mainCtrl (
  input  Op5,
  input  Op4,
  input  Op3,
  input  Op2,
  input  Op1,
  input  Op0,
  output WE,
  output St,
  output Ld,
  output Beq,
  output Bne,
  output J,
  output ExtOp
);

  wire and_2_out, and_3_out, and_7_out, and_8_out, not_1_out, not_2_out, not_3_out, not_4_out, not_5_out,
       not_6_out, not_7_out, not_8_out, not_9_out;

  not not_1 (not_1_out, Op3);
  not not_2 (not_2_out, Op5);
  and and_1 (St, Op5, Op3);
  not not_3 (not_3_out, Op3);
  not not_4 (not_4_out, Op3);
  not not_5 (not_5_out, Op0);
  not not_6 (not_6_out, Op3);
  not not_7 (not_7_out, Op1);
  not not_8 (not_8_out, Op2);
  not not_9 (not_9_out, Op3);
  and and_2 (and_2_out, not_1_out, Op1);
  and and_3 (and_3_out, not_2_out, Op3);
  and and_4 (Ld, Op5, not_3_out);
  and and_5 (Beq, not_4_out, Op2, not_5_out);
  and and_6 (Bne, not_6_out, not_7_out, Op0);
  and and_7 (and_7_out, not_8_out, Op0);
  and and_8 (and_8_out, not_9_out, Op2);
  or or_1 (WE, and_2_out, and_3_out);
  or or_2 (ExtOp, and_7_out, and_8_out);

  assign J = 1'b0;
endmodule

module opALU (
  input  Op5,
  input  Op4,
  input  Op3,
  input  Op2,
  input  Op1,
  input  Op0,
  output A3,
  output A2,
  output A1,
  output A0
);

  wire and_2_out, and_3_out, not_1_out, not_2_out, not_3_out, not_4_out;

  and and_1 (A3, Op3, Op2);
  not not_1 (not_1_out, Op3);
  not not_2 (not_2_out, Op1);
  not not_3 (not_3_out, Op0);
  not not_4 (not_4_out, Op3);
  and and_2 (and_2_out, not_1_out, not_2_out);
  and and_3 (and_3_out, Op1, not_3_out);
  or or_1 (A1, not_4_out, Op0);
  or or_2 (A2, and_2_out, and_3_out);

  assign A0 = 1'b0;
endmodule

module inputExt (
  input  sign,
  input  [15:0] A,
  output [31:0] O
);

  and and_1 (O[31], sign, A[15]);

  assign O[30:0] = {{15{O[31]}}, A};
endmodule
